// Logisim project Coe HW4.circ as structural Verilog: 8 circuits, main circuit Main
module Registe_File_16_bit (
  input  [2:0] RA,
  input  [2:0] RW,
  input  [2:0] RB,
  input  [15:0] BusW,
  input  Register_Write,
  input  Clock,
  input  in_7,
  output [15:0] BusA,
  output [15:0] out_9,
  output [15:0] out_10,
  output [15:0] out_11,
  output [15:0] out_12,
  output [15:0] out_13,
  output [15:0] out_14,
  output [15:0] out_15,
  output [15:0] BusB
);

  wire and_1_out, and_2_out, and_3_out, and_4_out, and_5_out, and_6_out, and_7_out, and_8_out,
       decoder_1_out0, decoder_1_out1, decoder_1_out2, decoder_1_out3, decoder_1_out4, decoder_1_out5,
       decoder_1_out6, decoder_1_out7;
  wire [15:0] register_1_q;

  Decoder #(.select(3), .enable("false")) decoder_1 (
    .out0(decoder_1_out0), .out1(decoder_1_out1), .out2(decoder_1_out2), .out3(decoder_1_out3),
    .out4(decoder_1_out4), .out5(decoder_1_out5), .out6(decoder_1_out6), .out7(decoder_1_out7), .sel(RW));
  and and_1 (and_1_out, decoder_1_out1, Register_Write);
  and and_2 (and_2_out, decoder_1_out2, Register_Write);
  and and_3 (and_3_out, decoder_1_out3, Register_Write);
  and and_4 (and_4_out, decoder_1_out4, Register_Write);
  and and_5 (and_5_out, decoder_1_out5, Register_Write);
  and and_6 (and_6_out, decoder_1_out6, Register_Write);
  and and_7 (and_7_out, decoder_1_out7, Register_Write);
  and and_8 (and_8_out, decoder_1_out0, Register_Write);
  Register #(.width(16)) register_1 (.D({16{1'b0}}), .en(and_8_out), .Q(register_1_q), .clk(Clock), .clr(in_7));
  Register #(.width(16)) R1 (.D(BusW), .en(and_1_out), .Q(out_9), .clk(Clock), .clr(in_7));
  Register #(.width(16)) R2 (.D(BusW), .en(and_2_out), .Q(out_10), .clk(Clock), .clr(in_7));
  Register #(.width(16)) R3 (.D(BusW), .en(and_3_out), .Q(out_11), .clk(Clock), .clr(in_7));
  Register #(.width(16)) R4 (.D(BusW), .en(and_4_out), .Q(out_12), .clk(Clock), .clr(in_7));
  Register #(.width(16)) R5 (.D(BusW), .en(and_5_out), .Q(out_13), .clk(Clock), .clr(in_7));
  Register #(.width(16)) R6 (.D(BusW), .en(and_6_out), .Q(out_14), .clk(Clock), .clr(in_7));
  Register #(.width(16)) R7 (.D(BusW), .en(and_7_out), .Q(out_15), .clk(Clock), .clr(in_7));
  Multiplexer #(.select(3), .width(16), .enable("false")) multiplexer_1 (
    .in0(register_1_q), .in1(out_9), .in2(out_10), .in3(out_11), .in4(out_12), .in5(out_13), .in6(out_14),
    .in7(out_15), .out(BusA), .sel(RA));
  Multiplexer #(.select(3), .width(16), .enable("false")) multiplexer_2 (
    .in0(register_1_q), .in1(out_9), .in2(out_10), .in3(out_11), .in4(out_12), .in5(out_13), .in6(out_14),
    .in7(out_15), .out(BusB), .sel(RB));
endmodule

module Main (
  input  in_1,
  input  in_2,
  input  in_3,
  output [1:0] out_4,
  output [1:0] out_5,
  output [15:0] out_6,
  output [15:0] out_7,
  output [15:0] out_8,
  output [15:0] out_9,
  output [4:0] out_10,
  output [15:0] out_11,
  output [4:0] out_12,
  output [2:0] out_13,
  output [15:0] out_14,
  output [2:0] out_15,
  output [15:0] out_16,
  output [2:0] out_17,
  output [15:0] out_18,
  output Over_flow,
  output Carry_out,
  output [2:0] out_21,
  output [15:0] R7,
  output [15:0] R6,
  output [15:0] R5,
  output [15:0] R4,
  output [15:0] R3,
  output [15:0] R2,
  output [15:0] R1
);

  wire ALUSrc, Clock_out, ExtOP, Mem_Rd, Mem_Wr, Reg_Dst, Reg_Wr, WB_data, Zero_Flag;
  wire [2:0] multiplexer_2_out;
  wire [4:0] PC__15_11;
  wire [10:0] register_1_q;
  wire [15:0] multiplexer_4_out, ram_1_data;

  PC_control_logic pc_control_logic_1 (.in_2(Zero_Flag), .out_3(out_4), .in_1(out_12));
  Clock Clock (.out(Clock_out));
  Multiplexer #(.select(2), .width(16), .enable("false")) multiplexer_1 (
    .in0(out_7), .in1({PC__15_11, out_13, out_15, out_10[4:2], out_5}), .in2(out_8), .out(out_6), .sel(out_4));  // open: in3
  Register #(.width(16)) register_1 (
    .D(out_6), .Q({PC__15_11, register_1_q}), .clk(Clock_out), .clr(in_3));  // open: en
  Adder #(.width(16)) adder_1 (.a(16'h1), .b({PC__15_11, register_1_q}), .out(out_7));  // open: cin, cout
  ROM #(.addrWidth(16), .dataWidth(16)) rom_1 (
    .addr({PC__15_11, register_1_q}), .data({out_12, out_13, out_15, out_10[4:2], out_5}), .sel(1'b1));
  Control_Unit control_unit_1 (
    .in_1(out_12), .Reg_Dst(Reg_Dst), .ExtOp(ExtOP), .Reg_Wr(Reg_Wr), .ALUSrc(ALUSrc), .Mem_Rd(Mem_Rd),
    .Mem_Wr(Mem_Wr), .WB_data(WB_data));
  ALU_Control alu_control_1 (.in_2(out_12), .in_1(out_5), .out_3(out_21));
  Registe_File_16_bit registe_file_16_bit_1 (
    .RA(out_13), .RW(multiplexer_2_out), .RB(out_15), .BusA(out_14), .BusB(out_18), .Register_Write(Reg_Wr),
    .Clock(Clock_out), .in_7(in_1), .BusW(multiplexer_4_out), .out_9(R1), .out_10(R2), .out_11(R3),
    .out_12(R4), .out_13(R5), .out_14(R6), .out_15(R7));
  Multiplexer #(.width(3), .enable("false")) multiplexer_2 (
    .in0(out_15), .in1(out_10[4:2]), .out(multiplexer_2_out), .sel(Reg_Dst));
  Extender extender_1 (.out_3(out_9), .in_1({out_10[4:2], out_5}), .in_2(ExtOP));
  Adder #(.width(16)) adder_2 (.a(out_7), .b(out_9), .out(out_8));  // open: cin, cout
  Multiplexer #(.width(16), .enable("false")) multiplexer_3 (.in0(out_18), .in1(out_9), .out(out_16), .sel(ALUSrc));
  ALU_16_bit alu_16_bit_1 (
    .Input_1(out_14), .Input_2(out_16), .Opeation(out_21), .out_4(out_11), .Carry_out(Carry_out),
    .Overflow(Over_flow), .Zero_Flag(Zero_Flag));
  RAM #(.addrWidth(16), .dataWidth(16), .bus("separate")) ram_1 (
    .addr(out_11), .din(out_18), .data(ram_1_data), .str(Mem_Wr), .clk(Clock_out), .ld(Mem_Rd), .clr(in_2));  // open: sel
  Multiplexer #(.width(16), .enable("false")) multiplexer_4 (
    .in0(out_11), .in1(ram_1_data), .out(multiplexer_4_out), .sel(WB_data));

  assign out_10[1:0] = out_5;
  assign out_17 = out_10[4:2];

  // Other names for the same wires on the sheet: Fun[1:0] = out_5; Op_code[4:0] = out_12; ALU_Opt[2:0] = out_21;
  //   PCSrc[1:0] = out_4

  // Notes on the sheet:
  //   contents of rom_1 (hex, n*v repeats v):
  //   6033 605e 14e 94d 94e 94f 4175 5175 5975 6975 7175 7975 c033 d000
endmodule

module ALU_16_bit (
  input  [15:0] Input_1,
  input  [2:0] Opeation,
  input  [15:0] Input_2,
  output [15:0] out_4,
  output Zero_Flag,
  output Overflow,
  output Carry_out
);

  wire alu_1_bit_1_borrow_out, alu_1_bit_1_carry_out, alu_1_bit_2_borrow_out, alu_1_bit_2_carry_out,
       alu_1_bit_3_borrow_out, alu_1_bit_3_carry_out, alu_1_bit_4_borrow_out, alu_1_bit_4_carry_out,
       alu_1_bit_5_borrow_out, alu_1_bit_5_carry_out, alu_1_bit_6_borrow_out, alu_1_bit_6_carry_out,
       alu_1_bit_7_borrow_out, alu_1_bit_7_carry_out, alu_1_bit_8_borrow_out, alu_1_bit_8_carry_out,
       alu_1_bit_9_borrow_out, alu_1_bit_9_carry_out, alu_1_bit_10_borrow_out, alu_1_bit_10_carry_out,
       alu_1_bit_11_borrow_out, alu_1_bit_11_carry_out, alu_1_bit_12_borrow_out, alu_1_bit_12_carry_out,
       alu_1_bit_13_borrow_out, alu_1_bit_13_carry_out, alu_1_bit_14_borrow_out, alu_1_bit_14_carry_out,
       alu_1_bit_15_borrow_out, alu_1_bit_15_carry_out, or_1_out, S00, S01, S02, S03, S04, S05, S06, S07,
       S08, S09, S10, S11, S12, S13, S14, S15;

  or or_1 (or_1_out, out_4[15], out_4[14], out_4[13], out_4[12], out_4[11], out_4[10], out_4[9], out_4[8], out_4[7], out_4[6], out_4[5], out_4[4], out_4[3], out_4[2], out_4[1], out_4[0]);
  not not_1 (Zero_Flag, or_1_out);
  ALU_1_bit alu_1_bit_1 (
    .Input_1(Input_1[0]), .Input_2(Input_2[0]), .Carry_in(1'b0), .Borrow_in(1'b0), .Output(out_4[0]),
    .SLT(S00), .operation(Opeation), .Borrow_out(alu_1_bit_1_borrow_out), .Less(S15),
    .Carry_out(alu_1_bit_1_carry_out));
  ALU_1_bit alu_1_bit_2 (
    .Input_1(Input_1[1]), .Input_2(Input_2[1]), .Carry_in(alu_1_bit_1_carry_out),
    .Borrow_in(alu_1_bit_1_borrow_out), .Output(out_4[1]), .SLT(S01), .operation(Opeation),
    .Borrow_out(alu_1_bit_2_borrow_out), .Less(1'b0), .Carry_out(alu_1_bit_2_carry_out));
  ALU_1_bit alu_1_bit_3 (
    .Input_1(Input_1[2]), .Input_2(Input_2[2]), .Carry_in(alu_1_bit_2_carry_out),
    .Borrow_in(alu_1_bit_2_borrow_out), .Output(out_4[2]), .SLT(S02), .operation(Opeation),
    .Borrow_out(alu_1_bit_3_borrow_out), .Less(1'b0), .Carry_out(alu_1_bit_3_carry_out));
  ALU_1_bit alu_1_bit_4 (
    .Input_1(Input_1[3]), .Input_2(Input_2[3]), .Carry_in(alu_1_bit_3_carry_out),
    .Borrow_in(alu_1_bit_3_borrow_out), .Output(out_4[3]), .SLT(S03), .operation(Opeation),
    .Borrow_out(alu_1_bit_4_borrow_out), .Less(1'b0), .Carry_out(alu_1_bit_4_carry_out));
  ALU_1_bit alu_1_bit_5 (
    .Input_1(Input_1[4]), .Input_2(Input_2[4]), .Carry_in(alu_1_bit_4_carry_out),
    .Borrow_in(alu_1_bit_4_borrow_out), .Output(out_4[4]), .SLT(S04), .operation(Opeation),
    .Borrow_out(alu_1_bit_5_borrow_out), .Less(1'b0), .Carry_out(alu_1_bit_5_carry_out));
  ALU_1_bit alu_1_bit_6 (
    .Input_1(Input_1[5]), .Input_2(Input_2[5]), .Carry_in(alu_1_bit_5_carry_out),
    .Borrow_in(alu_1_bit_5_borrow_out), .Output(out_4[5]), .SLT(S05), .operation(Opeation),
    .Borrow_out(alu_1_bit_6_borrow_out), .Less(1'b0), .Carry_out(alu_1_bit_6_carry_out));
  ALU_1_bit alu_1_bit_7 (
    .Input_1(Input_1[6]), .Input_2(Input_2[6]), .Carry_in(alu_1_bit_6_carry_out),
    .Borrow_in(alu_1_bit_6_borrow_out), .Output(out_4[6]), .SLT(S06), .operation(Opeation),
    .Borrow_out(alu_1_bit_7_borrow_out), .Less(1'b0), .Carry_out(alu_1_bit_7_carry_out));
  ALU_1_bit alu_1_bit_8 (
    .Input_1(Input_1[7]), .Input_2(Input_2[7]), .Carry_in(alu_1_bit_7_carry_out),
    .Borrow_in(alu_1_bit_7_borrow_out), .Output(out_4[7]), .SLT(S07), .operation(Opeation),
    .Borrow_out(alu_1_bit_8_borrow_out), .Less(1'b0), .Carry_out(alu_1_bit_8_carry_out));
  ALU_1_bit alu_1_bit_9 (
    .Input_1(Input_1[8]), .Input_2(Input_2[8]), .Carry_in(alu_1_bit_8_carry_out),
    .Borrow_in(alu_1_bit_8_borrow_out), .Output(out_4[8]), .SLT(S08), .operation(Opeation),
    .Borrow_out(alu_1_bit_9_borrow_out), .Less(1'b0), .Carry_out(alu_1_bit_9_carry_out));
  ALU_1_bit alu_1_bit_10 (
    .Input_1(Input_1[9]), .Input_2(Input_2[9]), .Carry_in(alu_1_bit_9_carry_out),
    .Borrow_in(alu_1_bit_9_borrow_out), .Output(out_4[9]), .SLT(S09), .operation(Opeation),
    .Borrow_out(alu_1_bit_10_borrow_out), .Less(1'b0), .Carry_out(alu_1_bit_10_carry_out));
  ALU_1_bit alu_1_bit_11 (
    .Input_1(Input_1[10]), .Input_2(Input_2[10]), .Carry_in(alu_1_bit_10_carry_out),
    .Borrow_in(alu_1_bit_10_borrow_out), .Output(out_4[10]), .SLT(S10), .operation(Opeation),
    .Borrow_out(alu_1_bit_11_borrow_out), .Less(1'b0), .Carry_out(alu_1_bit_11_carry_out));
  ALU_1_bit alu_1_bit_12 (
    .Input_1(Input_1[11]), .Input_2(Input_2[11]), .Carry_in(alu_1_bit_11_carry_out),
    .Borrow_in(alu_1_bit_11_borrow_out), .Output(out_4[11]), .SLT(S11), .operation(Opeation),
    .Borrow_out(alu_1_bit_12_borrow_out), .Less(1'b0), .Carry_out(alu_1_bit_12_carry_out));
  ALU_1_bit alu_1_bit_13 (
    .Input_1(Input_1[12]), .Input_2(Input_2[12]), .Carry_in(alu_1_bit_12_carry_out),
    .Borrow_in(alu_1_bit_12_borrow_out), .Output(out_4[12]), .SLT(S12), .operation(Opeation),
    .Borrow_out(alu_1_bit_13_borrow_out), .Less(1'b0), .Carry_out(alu_1_bit_13_carry_out));
  ALU_1_bit alu_1_bit_14 (
    .Input_1(Input_1[13]), .Input_2(Input_2[13]), .Carry_in(alu_1_bit_13_carry_out),
    .Borrow_in(alu_1_bit_13_borrow_out), .Output(out_4[13]), .SLT(S13), .operation(Opeation),
    .Borrow_out(alu_1_bit_14_borrow_out), .Less(1'b0), .Carry_out(alu_1_bit_14_carry_out));
  ALU_1_bit alu_1_bit_15 (
    .Input_1(Input_1[14]), .Input_2(Input_2[14]), .Carry_in(alu_1_bit_14_carry_out),
    .Borrow_in(alu_1_bit_14_borrow_out), .Output(out_4[14]), .SLT(S14), .operation(Opeation),
    .Borrow_out(alu_1_bit_15_borrow_out), .Less(1'b0), .Carry_out(alu_1_bit_15_carry_out));
  ALU_1_bit alu_1_bit_16 (
    .Input_1(Input_1[15]), .Input_2(Input_2[15]), .Carry_in(alu_1_bit_15_carry_out),
    .Borrow_in(alu_1_bit_15_borrow_out), .Output(out_4[15]), .SLT(S15), .operation(Opeation), .Less(1'b0),
    .Carry_out(Carry_out));  // open: Borrow_out
  xor xor_1 (Overflow, alu_1_bit_15_carry_out, Carry_out);

  // Other names for the same wires on the sheet: A00 = Input_1[0]; A01 = Input_1[1]; A02 = Input_1[2];
  //   A03 = Input_1[3]; A04 = Input_1[4]; A05 = Input_1[5]; A06 = Input_1[6]; A07 = Input_1[7]; A08 = Input_1[8];
  //   A09 = Input_1[9]; A10 = Input_1[10]; A11 = Input_1[11]; A12 = Input_1[12]; A13 = Input_1[13]; A14 = Input_1[14];
  //   A15 = Input_1[15]; B00 = Input_2[0]; B01 = Input_2[1]; B02 = Input_2[2]; B03 = Input_2[3]; B04 = Input_2[4];
  //   B05 = Input_2[5]; B06 = Input_2[6]; B07 = Input_2[7]; B08 = Input_2[8]; B09 = Input_2[9]; B10 = Input_2[10];
  //   B11 = Input_2[11]; B12 = Input_2[12]; B13 = Input_2[13]; B14 = Input_2[14]; B15 = Input_2[15]; O00 = out_4[0];
  //   O01 = out_4[1]; O02 = out_4[2]; O03 = out_4[3]; O04 = out_4[4]; O05 = out_4[5]; O06 = out_4[6]; O07 = out_4[7];
  //   O08 = out_4[8]; O09 = out_4[9]; O10 = out_4[10]; O11 = out_4[11]; O12 = out_4[12]; O13 = out_4[13];
  //   O14 = out_4[14]; O15 = out_4[15]; P01[2:0] = Opeation
endmodule

module ALU_1_bit (
  input  Input_2,
  input  Input_1,
  input  Carry_in,
  input  [2:0] operation,
  input  Borrow_in,
  input  Less,
  output Output,
  output SLT,
  output Carry_out,
  output Borrow_out
);

  wire adder_1_out, and_1_out, comparator_1_eq, nor_1_out, or_1_out, xor_1_out;

  Comparator #(.width(1)) comparator_1 (.a(Input_1), .b(Input_2), .eq(comparator_1_eq));  // open: gt, lt
  and and_1 (and_1_out, Input_1, Input_2);
  or or_1 (or_1_out, Input_1, Input_2);
  xor xor_1 (xor_1_out, Input_1, Input_2);
  nor nor_1 (nor_1_out, Input_1, Input_2);
  Adder #(.width(1)) adder_1 (.a(Input_1), .b(Input_2), .out(adder_1_out), .cin(Carry_in), .cout(Carry_out));
  Subtractor #(.width(1)) subtractor_1 (.a(Input_1), .b(Input_2), .out(SLT), .bin(Borrow_in), .bout(Borrow_out));
  Multiplexer #(.select(3), .enable("false")) multiplexer_1 (
    .in0(and_1_out), .in1(or_1_out), .in2(xor_1_out), .in3(nor_1_out), .in4(adder_1_out), .in5(SLT),
    .in6(comparator_1_eq), .in7(Less), .out(Output), .sel(operation));
endmodule

// E
module Extender (
  input  [4:0] in_1,
  input  in_2,
  output [15:0] out_3
);

  wire [15:0] bit_extender_1_out, bit_extender_2_out;

  assign bit_extender_1_out = {{11{1'b0}}, in_1};  // Bit_Extender bit_extender_1
  assign bit_extender_2_out = {{11{in_1[4]}}, in_1};  // Bit_Extender bit_extender_2
  Multiplexer #(.width(16), .enable("false")) multiplexer_1 (
    .in0(bit_extender_1_out), .in1(bit_extender_2_out), .out(out_3), .sel(in_2));
endmodule

// Main Control
module Control_Unit (
  input  [4:0] in_1,
  output Reg_Dst,
  output ExtOp,
  output Mem_Rd,
  output WB_data,
  output Mem_Wr,
  output ALUSrc,
  output Reg_Wr
);

  wire ADDI, ANDI, BEQ, BNE, NADDI, NORI, or_3_out, or_4_out, ORI, R_type0, R_type1, SEQI, SLTI, XORI;

  or or_1 (Reg_Dst, R_type0, R_type1);
  or or_2 (Reg_Wr, Reg_Dst, ANDI, ORI, XORI, NORI, ADDI, NADDI, SEQI, SLTI, Mem_Rd);
  Decoder #(.select(5), .enable("false")) decoder_1 (
    .out0(R_type0), .out1(R_type1), .out8(ANDI), .out9(ORI), .out10(XORI), .out11(NORI), .out12(ADDI),
    .out13(NADDI), .out14(SEQI), .out15(SLTI), .out16(Mem_Rd), .out17(Mem_Wr), .out24(BEQ), .out25(BNE),
    .sel(in_1));  // open: out2, out3, out4, out5, out6, out7, out18, out19, out20, out21, out22, out23, out26, out27, out28, out29, out30, out31
  or or_3 (or_3_out, ANDI, ORI, XORI, NORI);
  not not_1 (ExtOp, or_3_out);
  or or_4 (or_4_out, R_type0, R_type1, BEQ, BNE);
  not not_2 (ALUSrc, or_4_out);

  assign WB_data = Mem_Rd;

  // Other names for the same wires on the sheet: LH = Mem_Rd; SH = Mem_Wr
endmodule

module ALU_Control (
  input  [1:0] in_1,
  input  [4:0] in_2,
  output [2:0] out_3
);

  wire [2:0] adder_1_out, bit_extender_1_out;

  assign bit_extender_1_out = {{1{1'b0}}, in_1};  // Bit_Extender bit_extender_1
  Adder #(.width(3)) adder_1 (.a(3'b100), .b(bit_extender_1_out), .out(adder_1_out));  // open: cin, cout
  Multiplexer #(.select(5), .width(3), .enable("false")) multiplexer_1 (
    .in0(bit_extender_1_out), .in1(adder_1_out), .in8(in_2[2:0]), .in9(in_2[2:0]), .in10(in_2[2:0]),
    .in11(in_2[2:0]), .in12(in_2[2:0]), .in13(in_2[2:0]), .in14(in_2[2:0]), .in15(in_2[2:0]), .in16(3'b100),
    .in17(3'b100), .in24(3'b111), .in25(3'b111), .out(out_3), .sel(in_2));  // open: in2, in3, in4, in5, in6, in7, in18, in19, in20, in21, in22, in23, in26, in27, in28, in29, in30, in31

  // Other names for the same wires on the sheet: I[2:0] = in_2[2:0]
endmodule

// PC control
module PC_control_logic (
  input  [4:0] in_1,
  input  in_2,
  output [1:0] out_3
);

  wire and_1_out, and_2_out, decoder_1_out24, decoder_1_out25, not_1_out;

  Decoder #(.select(5), .enable("false")) decoder_1 (
    .out24(decoder_1_out24), .out25(decoder_1_out25), .out26(out_3[0]), .sel(in_1));  // open: out0, out1, out2, out3, out4, out5, out6, out7, out8, out9, out10, out11, out12, out13, out14, out15, out16, out17, out18, out19, out20, out21, out22, out23, out27, out28, out29, out30, out31
  and and_1 (and_1_out, decoder_1_out24, in_2);
  not not_1 (not_1_out, in_2);
  and and_2 (and_2_out, decoder_1_out25, not_1_out);
  or or_1 (out_3[1], and_1_out, and_2_out);
endmodule
